// Logisim project ITC_logism_tutorial.circ as structural Verilog: 2 circuits, main circuit main
module main (
  input  [7:0] in_1,
  input  [7:0] in_2,
  output [7:0] out_3
);

  // Probe on in_2
  // Probe on in_1
  Adder adder_1 (.a(in_1), .b(in_2), .out(out_3));  // open: cin, cout
  // Probe on out_3
endmodule

module ram1 (
  input  in_1
);

  wire clock_1_out;
  wire [7:0] counter_1_q, ram_1_dout, ram_2_dout;

  Counter counter_1 (.Q(counter_1_q), .clk(clock_1_out));  // open: load, D, count, carry, up, clr
  Clock clock_1 (.out(clock_1_out));
  RAM #(.databus("bibusControlled"), .trigger("high")) ram_1 (
    .addr(counter_1_q), .we(in_1), .oe(clock_1_out), .dout(ram_1_dout));  // open: din
  RAM #(.databus("bibusControlled"), .trigger("high")) ram_2 (
    .addr(counter_1_q), .we(in_1), .oe(clock_1_out), .dout(ram_2_dout));  // open: din
  Register register_1 (.D(ram_1_dout), .en(in_1), .clk(clock_1_out));  // open: Q, clr
  Register register_2 (.D(ram_2_dout), .en(in_1), .clk(clock_1_out));  // open: Q, clr
endmodule
