// Logisim project VideoAssignment.circ as structural Verilog: 1 circuit, main circuit main
module main (
  input  in_1
);

  wire bcd_to_7_segment_decoder_3_p1, binary_to_bcd_converter_1_p2, binary_to_bcd_converter_1_p4,
       clock_1_out, comparator_1_eq, comparator_2_eq, comparator_3_eq, comparator_4_eq, comparator_5_eq,
       j_k_ff_1_q, j_k_ff_2_q;
  wire [7:0] counter_1_q;

  Clock clock_1 (.out(clock_1_out));
  Counter #(.max('hf)) counter_1 (.Q(counter_1_q), .clk(clock_1_out), .clr(in_1));  // open: load, D, count, carry, up
  // BCD_to_7_Segment_decoder bcd_to_7_segment_decoder_1: pin names not known
  _7_Segment_Display u_7_segment_display_1 ();  // open: g, f, a, b, e, d, c, dp
  // Binary_to_BCD_converter #(.binvalue(8)) binary_to_bcd_converter_1: pin names not known; wires that end beside it: counter_1_q, binary_to_bcd_converter_1_p2, binary_to_bcd_converter_1_p2, binary_to_bcd_converter_1_p4
  Comparator comparator_1 (.a({8{1'b0}}), .b(counter_1_q), .eq(comparator_1_eq));  // open: gt, lt
  Comparator comparator_2 (.a(8'h2), .b(counter_1_q), .eq(comparator_2_eq));  // open: gt, lt
  Comparator comparator_3 (.a(8'ha), .b(counter_1_q), .eq(comparator_3_eq));  // open: gt, lt
  Comparator comparator_4 (.a(8'h5), .b(counter_1_q), .eq(comparator_4_eq));  // open: gt, lt
  Comparator comparator_5 (.a(8'ha), .b(counter_1_q), .eq(comparator_5_eq));  // open: gt, lt
  // BCD_to_7_Segment_decoder bcd_to_7_segment_decoder_2: pin names not known; wires that end beside it: binary_to_bcd_converter_1_p4
  // BCD_to_7_Segment_decoder bcd_to_7_segment_decoder_3: pin names not known; wires that end beside it: bcd_to_7_segment_decoder_3_p1
  _7_Segment_Display u_7_segment_display_2 ();  // open: g, f, a, b, e, d, c, dp
  _7_Segment_Display u_7_segment_display_3 ();  // open: g, f, a, b, e, d, c, dp
  LED led_1 (.in(comparator_1_eq));
  J_K_Flip_Flop j_k_ff_1 (
    .J(comparator_2_eq), .K(comparator_3_eq), .clk(clock_1_out), .Q(j_k_ff_1_q));  // open: Qn, preset, reset
  J_K_Flip_Flop j_k_ff_2 (
    .J(comparator_4_eq), .K(comparator_5_eq), .clk(clock_1_out), .Q(j_k_ff_2_q));  // open: Qn, preset, reset
  // Buzzer #(.vol_width(14)) buzzer_1: pin names not known; wires that end beside it: bcd_to_7_segment_decoder_3_p1, 14'h2710, comparator_1_eq, 14'h1fff
  // Digital_Oscilloscope #(.nState(20)) digital_oscilloscope_1: pin names not known; wires that end beside it: clock_1_out, comparator_1_eq, j_k_ff_1_q, j_k_ff_2_q
  // Buzzer #(.vol_width(14)) buzzer_2: pin names not known; wires that end beside it: 14'h1333, j_k_ff_1_q, 14'h1fff
  // Buzzer #(.vol_width(14)) buzzer_3: pin names not known; wires that end beside it: 14'h1fff, j_k_ff_2_q, 14'h1066
endmodule
